// Logisim project 005_Basic_MPU.circ as structural Verilog: 4 circuits, main circuit main
module main (
);

  ProgramCounter programcounter_1 ();  // open: Enable, Clock, PC
  ArithmeticLogicUnit arithmeticlogicunit_1 ();  // open: Res, A, B, Ci, MUX, Status
endmodule

// GPR
module Register (
  input  I0,
  input  I1,
  input  I2,
  input  I3,
  input  I4,
  input  I5,
  input  I6,
  input  I7,
  input  R_w,
  input  Clock,
  input  Enable,
  input  Reset,
  output O0,
  output O1,
  output O2,
  output O3,
  output O4,
  output O5,
  output O6,
  output O7
);

  wire I0_t, I1_t, I2_t, I3_t, I4_t, I5_t, I6_t, I7_t, not_1_out, O0_t, O1_t, O2_t, O3_t, O4_t, O5_t, O6_t,
       O7_t;

  assign I0_t = not_1_out ? I0 : 1'bz;  // Controlled_Buffer controlled_buffer_1
  assign I1_t = not_1_out ? I1 : 1'bz;  // Controlled_Buffer controlled_buffer_2
  assign I2_t = not_1_out ? I2 : 1'bz;  // Controlled_Buffer controlled_buffer_3
  assign I3_t = not_1_out ? I3 : 1'bz;  // Controlled_Buffer controlled_buffer_4
  assign I4_t = not_1_out ? I4 : 1'bz;  // Controlled_Buffer controlled_buffer_5
  assign I5_t = not_1_out ? I5 : 1'bz;  // Controlled_Buffer controlled_buffer_6
  assign I6_t = not_1_out ? I6 : 1'bz;  // Controlled_Buffer controlled_buffer_7
  assign I7_t = not_1_out ? I7 : 1'bz;  // Controlled_Buffer controlled_buffer_8
  not not_1 (not_1_out, R_w);
  assign O0 = R_w ? O0_t : 1'bz;  // Controlled_Buffer controlled_buffer_9
  assign O1 = R_w ? O1_t : 1'bz;  // Controlled_Buffer controlled_buffer_10
  assign O2 = R_w ? O2_t : 1'bz;  // Controlled_Buffer controlled_buffer_11
  assign O3 = R_w ? O3_t : 1'bz;  // Controlled_Buffer controlled_buffer_12
  assign O4 = R_w ? O4_t : 1'bz;  // Controlled_Buffer controlled_buffer_13
  assign O5 = R_w ? O5_t : 1'bz;  // Controlled_Buffer controlled_buffer_14
  assign O6 = R_w ? O6_t : 1'bz;  // Controlled_Buffer controlled_buffer_15
  assign O7 = R_w ? O7_t : 1'bz;  // Controlled_Buffer controlled_buffer_16
  D_Flip_Flop d_ff_1 (.clk(Clock), .D(I7_t), .Q(O7_t), .en(Enable), .reset(Reset));  // open: Qn, preset
  D_Flip_Flop d_ff_2 (.clk(Clock), .D(I6_t), .Q(O6_t), .en(Enable), .reset(Reset));  // open: Qn, preset
  D_Flip_Flop d_ff_3 (.clk(Clock), .D(I5_t), .Q(O5_t), .en(Enable), .reset(Reset));  // open: Qn, preset
  D_Flip_Flop d_ff_4 (.clk(Clock), .D(I4_t), .Q(O4_t), .en(Enable), .reset(Reset));  // open: Qn, preset
  D_Flip_Flop d_ff_5 (.clk(Clock), .D(I3_t), .Q(O3_t), .en(Enable), .reset(Reset));  // open: Qn, preset
  D_Flip_Flop d_ff_6 (.clk(Clock), .D(I2_t), .Q(O2_t), .en(Enable), .reset(Reset));  // open: Qn, preset
  D_Flip_Flop d_ff_7 (.clk(Clock), .D(I1_t), .Q(O1_t), .en(Enable), .reset(Reset));  // open: Qn, preset
  D_Flip_Flop d_ff_8 (.clk(Clock), .D(I0_t), .Q(O0_t), .en(Enable), .reset(Reset));  // open: Qn, preset
endmodule

// PC
module ProgramCounter (
  input  Enable,
  input  Clock,
  output [15:0] PC
);

  Counter #(.width(16), .max('hffff)) counter_1 (.count(Enable), .Q(PC), .clk(Clock));  // open: load, D, carry, clr
endmodule

// ALU
module ArithmeticLogicUnit (
  input  Ci,
  input  [7:0] A,
  input  [7:0] B,
  input  [3:0] MUX,
  output [7:0] Res,
  output [7:0] Status
);

  wire adder_1_cout, and_2_out, or_2_out, subtractor_1_bout;
  wire [7:0] adder_1_out, and_1_out, divider_1_out, multiplier_1_out, negator_1_out, negator_2_out, or_1_out,
       shifter_1_out, shifter_2_out, subtractor_1_out, xor_1_out;

  Multiplexer #(.enable("false")) multiplexer_1 (
    .in0(adder_1_cout), .in1(subtractor_1_bout), .out(Status[7]), .sel(and_2_out));
  Adder adder_1 (.a(A), .b(B), .out(adder_1_out), .cin(Ci), .cout(adder_1_cout));
  Subtractor subtractor_1 (.a(A), .b(B), .out(subtractor_1_out), .bin(Ci), .bout(subtractor_1_bout));
  Multiplier multiplier_1 (.a(A), .b(B), .out(multiplier_1_out));  // open: cin, cout
  Divider divider_1 (.a(A), .b(B), .out(divider_1_out));  // open: upper, rem
  Negator negator_1 (.in(A), .out(negator_1_out));
  Negator negator_2 (.in(B), .out(negator_2_out));
  assign and_1_out = A & B;  // AND_Gate and_1, 8 bits wide
  assign or_1_out = A | B;  // OR_Gate or_1, 8 bits wide
  assign xor_1_out = A ^ B;  // XOR_Gate xor_1, 8 bits wide
  Shifter shifter_1 (.in(A), .\dist (B[2:0]), .out(shifter_1_out));
  Shifter #(.shift("lr")) shifter_2 (.in(A), .\dist (B[2:0]), .out(shifter_2_out));
  and and_2 (and_2_out, ~MUX[0], MUX[1], ~MUX[2], ~MUX[3]);  // AND_Gate
  Multiplexer #(.select(4), .width(8), .enable("false")) multiplexer_2 (
    .in0(A), .in1(adder_1_out), .in2(subtractor_1_out), .in3(multiplier_1_out), .in4(divider_1_out),
    .in5(negator_1_out), .in6(negator_2_out), .in8(and_1_out), .in9(or_1_out), .in10(xor_1_out),
    .in11(shifter_1_out), .in12(shifter_2_out), .out(Res), .sel(MUX));  // open: in7, in13, in14, in15
  or or_2 (or_2_out, Res[0], Res[1], Res[2], Res[3], Res[4], Res[5], Res[6], Res[7]);
  not not_1 (Status[0], or_2_out);
  xor odd_parity_1 (Status[2], Res[0], Res[1], Res[2], Res[3], Res[4], Res[5], Res[6], Res[7]);

  assign Status[1] = Res[7];

  // Other names for the same wires on the sheet: CO_B = Status[7]

  // Notes on the sheet:
  //   ALU Operations
  //   0001       Addition
  //   0010       Subtraction
  //   0011      Multiplication
  //   0100      Division
  //   0000      PassThrough
  //   0101      NegateA
  //   0110      NegateB
  //   1000       Bitwise AND
  //   1001      Bitwise OR
  //   1010      Bitwise XOR
  //   1011      Shift Left
  //   1100      Shift Right
endmodule
